// Logisim project terminal.circ as structural Verilog: 15 circuits, main circuit main
module Reg (
  input  Left,
  input  Right,
  input  first_pos,
  output SET4,
  output SET3,
  output SET2,
  output SET1
);

  wire and_1_out, and_2_out, and_3_out, and_4_out, and_5_out, and_6_out, j_k_ff_1_q, j_k_ff_1_qn, j_k_ff_2_q,
       j_k_ff_2_qn, j_k_ff_3_q, j_k_ff_3_qn, not_1_out, not_2_out, not_3_out, or_1_out, or_2_out, or_3_out,
       or_4_out;

  and and_1 (and_1_out, j_k_ff_3_qn, Right);
  and and_2 (and_2_out, Left, or_3_out);
  or or_1 (or_1_out, and_1_out, and_2_out);
  J_K_Flip_Flop #(.trigger("falling")) j_k_ff_1 (
    .J(1'b1), .K(1'b1), .clk(or_1_out), .Q(j_k_ff_1_q), .Qn(j_k_ff_1_qn), .preset(first_pos));  // open: reset
  and and_3 (and_3_out, and_1_out, j_k_ff_1_q);
  and and_4 (and_4_out, j_k_ff_1_qn, and_2_out);
  or or_2 (or_2_out, and_3_out, and_4_out);
  J_K_Flip_Flop #(.trigger("falling")) j_k_ff_2 (
    .J(1'b1), .K(1'b1), .clk(or_2_out), .Q(j_k_ff_2_q), .Qn(j_k_ff_2_qn), .reset(first_pos));  // open: preset
  and and_5 (and_5_out, and_1_out, j_k_ff_1_q, j_k_ff_2_q);
  and and_6 (and_6_out, j_k_ff_2_qn, j_k_ff_1_qn, and_2_out);
  or or_3 (or_3_out, j_k_ff_2_q, j_k_ff_3_q);
  or or_4 (or_4_out, and_5_out, and_6_out);
  J_K_Flip_Flop #(.trigger("falling")) j_k_ff_3 (
    .J(1'b1), .K(1'b1), .clk(or_4_out), .Q(j_k_ff_3_q), .Qn(j_k_ff_3_qn), .reset(first_pos));  // open: preset
  not not_1 (not_1_out, j_k_ff_3_q);
  not not_2 (not_2_out, j_k_ff_2_q);
  not not_3 (not_3_out, j_k_ff_1_q);
  and and_7 (SET1, not_1_out, not_2_out, j_k_ff_1_q);
  and and_8 (SET2, not_1_out, j_k_ff_2_q, not_3_out);
  and and_9 (SET3, not_1_out, j_k_ff_2_q, j_k_ff_1_q);
  and and_10 (SET4, j_k_ff_3_q, not_2_out, not_3_out);
endmodule

module main (
  input  Input_1,
  input  Input_2,
  input  Input_3,
  input  Input_4
);

  wire and_1_out, and_2_out, and_3_out, and_4_out, Button_1_out, Button_2_out, clock_1_out, Generator_1_clk,
       Generator_1_priem_out, obrabotka_1_delete, obrabotka_1_enter, obrabotka_1_left_cursor,
       obrabotka_1_right_cursor, or_1_out, or_2_out, or_3_out, or_4_out, or_5_out, or_6_out, Reg_1_set1,
       Reg_1_set2, Reg_1_set3, Reg_1_set4;
  wire [3:0] ascii_to_bcd_4_bcd, L_7_Segment_Display_1_p1, L_7_Segment_Display_1_p3, L_7_Segment_Display_2_p3;
  wire [7:0] DipSwitch_1_sw8, Display_1_disp1, Display_1_disp2, Display_1_disp3, Display_1_disp4,
       obrabotka_1_res;

  DipSwitch DipSwitch_1 (
    .sw1(DipSwitch_1_sw8[7]), .sw2(DipSwitch_1_sw8[6]), .sw3(DipSwitch_1_sw8[5]), .sw4(DipSwitch_1_sw8[4]),
    .sw5(DipSwitch_1_sw8[3]), .sw6(DipSwitch_1_sw8[2]), .sw7(DipSwitch_1_sw8[1]), .sw8(DipSwitch_1_sw8[0]));
  Clock clock_1 (.out(clock_1_out));
  obrabotka obrabotka_1 (
    .inp(DipSwitch_1_sw8), .clk(Generator_1_clk), .Reset_1(Input_1), .Reset_2(Input_2), .Reset_3(Input_3),
    .Reset_4(Input_4), .Priem(Generator_1_priem_out), .res(obrabotka_1_res),
    .Left_Cursor(obrabotka_1_left_cursor), .Right_Cursor(obrabotka_1_right_cursor),
    .Delete(obrabotka_1_delete), .Enter(obrabotka_1_enter));
  Generator Generator_1 (
    .gen_in(clock_1_out), .Priem_in(Button_2_out), .clk(Generator_1_clk), .Priem_out(Generator_1_priem_out));
  Button Button_1 (.out(Button_1_out));
  Button Button_2 (.out(Button_2_out));
  or or_1 (or_1_out, Button_1_out, obrabotka_1_enter);
  Reg Reg_1 (
    .Left(obrabotka_1_left_cursor), .Right(obrabotka_1_right_cursor), .first_pos(or_1_out),
    .SET4(Reg_1_set4), .SET3(Reg_1_set3), .SET2(Reg_1_set2), .SET1(Reg_1_set1));
  or or_2 (or_2_out, obrabotka_1_enter, Button_1_out);
  and and_1 (and_1_out, Reg_1_set4, obrabotka_1_delete);
  and and_2 (and_2_out, Reg_1_set3, obrabotka_1_delete);
  and and_3 (and_3_out, Reg_1_set2, obrabotka_1_delete);
  and and_4 (and_4_out, Reg_1_set1, obrabotka_1_delete);
  or or_3 (or_3_out, and_4_out, or_2_out);
  or or_4 (or_4_out, and_3_out, or_2_out);
  or or_5 (or_5_out, and_2_out, or_2_out);
  or or_6 (or_6_out, and_1_out, or_2_out);
  Display Display_1 (
    .inp(obrabotka_1_res), .clk(Generator_1_clk), .SET1(Reg_1_set1), .Reset_1(or_3_out), .SET2(Reg_1_set2),
    .Reset_2(or_4_out), .SET3(Reg_1_set3), .Reset_3(or_5_out), .SET4(Reg_1_set4), .Reset_4(or_6_out),
    .Priem(Generator_1_priem_out), .Disp1(Display_1_disp1), .Disp2(Display_1_disp2), .Disp3(Display_1_disp3),
    .Disp4(Display_1_disp4));
  // BCD_to_7_Segment_decoder bcd_to_7_segment_decoder_1: pin names not known
  // _7_Segment_Display L_7_Segment_Display_1: pin names not known; wires that end beside it: L_7_Segment_Display_1_p1, Reg_1_set1, L_7_Segment_Display_1_p3
  // BCD_to_7_Segment_decoder bcd_to_7_segment_decoder_2: pin names not known
  // _7_Segment_Display L_7_Segment_Display_2: pin names not known; wires that end beside it: L_7_Segment_Display_1_p3, Reg_1_set2, L_7_Segment_Display_2_p3
  ascii_to_bcd ascii_to_bcd_1 (.ASCII(Display_1_disp1), .BCD(L_7_Segment_Display_1_p1));
  ascii_to_bcd ascii_to_bcd_2 (.ASCII(Display_1_disp2), .BCD(L_7_Segment_Display_1_p3));
  ascii_to_bcd ascii_to_bcd_3 (.ASCII(Display_1_disp3), .BCD(L_7_Segment_Display_2_p3));
  ascii_to_bcd ascii_to_bcd_4 (.ASCII(Display_1_disp4), .BCD(ascii_to_bcd_4_bcd));
  // BCD_to_7_Segment_decoder bcd_to_7_segment_decoder_3: pin names not known
  // BCD_to_7_Segment_decoder bcd_to_7_segment_decoder_4: pin names not known
  // _7_Segment_Display L_7_Segment_Display_3: pin names not known; wires that end beside it: L_7_Segment_Display_2_p3, Reg_1_set3, ascii_to_bcd_4_bcd
  _7_Segment_Display L_7_Segment_Display_4 (.dp(Reg_1_set4));  // open: g, f, a, b, e, d, c
endmodule

module Display (
  input  [7:0] inp,
  input  clk,
  input  SET1,
  input  Reset_1,
  input  SET2,
  input  Reset_2,
  input  SET3,
  input  Reset_3,
  input  SET4,
  input  Reset_4,
  input  Priem,
  output [7:0] Disp1,
  output [7:0] Disp2,
  output [7:0] Disp3,
  output [7:0] Disp4
);

  wire and_1_out, and_2_out, and_3_out, and_4_out, and_5_out, delay2_1_del2, delay3_1_del3, nor_1_out,
       nor_2_out, nor_3_out, nor_4_out, not_1_out, or_1_out;

  or or_1 (or_1_out, inp[0], inp[1], inp[2], inp[3], inp[4], inp[5], inp[6], inp[7]);
  delay2 delay2_1 (.clk(clk), .priem(Priem), .del2(delay2_1_del2));
  not not_1 (not_1_out, delay3_1_del3);
  delay3 delay3_1 (.clk(clk), .priem(Priem), .del3(delay3_1_del3));
  and and_1 (and_1_out, delay2_1_del2, not_1_out, or_1_out);
  and and_2 (and_2_out, nor_1_out, and_1_out, SET1);
  Register register_1 (.D(inp), .en(SET1), .clk(and_2_out), .Q(Disp1), .clr(Reset_1));
  nor nor_1 (nor_1_out, Disp1[0], Disp1[1], Disp1[2], Disp1[3], Disp1[4], Disp1[5], Disp1[6], Disp1[7]);
  Register register_2 (.D(inp), .en(SET2), .clk(and_3_out), .Q(Disp2), .clr(Reset_2));
  and and_3 (and_3_out, nor_2_out, and_1_out, SET2);
  nor nor_2 (nor_2_out, Disp2[0], Disp2[1], Disp2[2], Disp2[3], Disp2[4], Disp2[5], Disp2[6], Disp2[7]);
  Register register_3 (.D(inp), .en(SET3), .clk(and_4_out), .Q(Disp3), .clr(Reset_3));
  and and_4 (and_4_out, nor_3_out, and_1_out, SET3);
  nor nor_3 (nor_3_out, Disp3[0], Disp3[1], Disp3[2], Disp3[3], Disp3[4], Disp3[5], Disp3[6], Disp3[7]);
  Register register_4 (.D(inp), .en(SET4), .clk(and_5_out), .Q(Disp4), .clr(Reset_4));
  and and_5 (and_5_out, nor_4_out, and_1_out, SET4);
  nor nor_4 (nor_4_out, Disp4[0], Disp4[1], Disp4[2], Disp4[3], Disp4[4], Disp4[5], Disp4[6], Disp4[7]);
endmodule

module obrabotka (
  input  [7:0] inp,
  input  clk,
  input  Reset_1,
  input  Reset_2,
  input  Reset_3,
  input  Reset_4,
  input  Priem,
  output [7:0] res,
  output Left_Cursor,
  output Right_Cursor,
  output Delete,
  output Enter
);

  wire and_1_out, and_2_out, and_3_out, and_4_out, Cont_seq_1_esc1, Cont_seq_1_esc2, Cont_seq_1_esc3,
       delay1_1_del1, delay2_1_del2, gate_1_right_cursor, not_1_out, or_1_out, or_2_out, or_3_out, or_4_out,
       or_5_out, to_save_1_yc, to_save_1_yp;
  wire [7:0] register_1_q, register_2_q, register_3_q, register_4_q;

  delay1 delay1_1 (.clk(clk), .priem(Priem), .del1(delay1_1_del1));
  delay2 delay2_1 (.clk(clk), .priem(Priem), .del2(delay2_1_del2));
  or or_1 (or_1_out, inp[0], inp[1], inp[2], inp[3], inp[4], inp[5], inp[6], inp[7]);
  and and_1 (and_1_out, delay1_1_del1, ~delay2_1_del2);  // AND_Gate
  Register register_1 (.D(inp), .clk(and_2_out), .Q(register_1_q), .clr(or_2_out));  // open: en
  and and_2 (and_2_out, and_1_out, to_save_1_yp, or_1_out);
  and and_3 (and_3_out, not_1_out, and_1_out, clk);
  or or_2 (or_2_out, and_3_out, Reset_1);
  Register register_2 (.D(register_1_q), .clk(and_2_out), .Q(register_2_q), .clr(or_3_out));  // open: en
  or or_3 (or_3_out, and_3_out, Reset_2);
  not not_1 (not_1_out, to_save_1_yp);
  and and_4 (and_4_out, not_1_out, or_1_out, to_save_1_yc);
  Register register_3 (.D(register_2_q), .clk(and_2_out), .Q(register_3_q), .clr(or_4_out));  // open: en
  or or_4 (or_4_out, and_3_out, Reset_3);
  Register register_4 (.D(register_3_q), .clk(and_2_out), .Q(register_4_q), .clr(or_5_out));  // open: en
  or or_5 (or_5_out, and_3_out, Reset_4);
  gate gate_1 (.clk(clk), .sig(and_4_out), .inp(inp), .Priem(Priem), .res(res), .right_cursor(gate_1_right_cursor));
  Comands Comands_1 (
    .right_from_gate(gate_1_right_cursor), .Trig_1(register_1_q), .Trig_2(register_2_q),
    .Trig_3(register_3_q), .Trig_4(register_4_q), .clk(clk), .Priem(Priem), .Left_Cursor(Left_Cursor),
    .Right_Cursor(Right_Cursor), .Delete(Delete), .Enter(Enter));
  Cont_seq Cont_seq_1 (
    .Trig_1(register_1_q), .Trig_2(register_2_q), .Trig_3(register_3_q), .clk(clk), .Priem(Priem),
    .ESC1(Cont_seq_1_esc1), .ESC2(Cont_seq_1_esc2), .ESC3(Cont_seq_1_esc3));
  to_save to_save_1 (
    .inp(inp), .ESC1(Cont_seq_1_esc1), .ESC2(Cont_seq_1_esc2), .ESC3(Cont_seq_1_esc3), .YP(to_save_1_yp),
    .YC(to_save_1_yc));
endmodule

module gate (
  input  clk,
  input  sig,
  input  [7:0] inp,
  input  Priem,
  output [7:0] res,
  output right_cursor
);

  wire and_1_out, delay3_1_del3, delay4_1_del4, not_1_out;

  and and_1 (and_1_out, clk, sig);
  and and_2 (res[0], inp[0], and_1_out);
  and and_3 (res[1], inp[1], and_1_out);
  and and_4 (res[2], inp[2], and_1_out);
  and and_5 (res[3], inp[3], and_1_out);
  and and_6 (res[4], inp[4], and_1_out);
  and and_7 (res[5], inp[5], and_1_out);
  and and_8 (res[6], inp[6], and_1_out);
  and and_9 (res[7], inp[7], and_1_out);
  delay3 delay3_1 (.clk(clk), .priem(Priem), .del3(delay3_1_del3));
  not not_1 (not_1_out, delay4_1_del4);
  and and_10 (right_cursor, delay3_1_del3, not_1_out, sig);
  delay4 delay4_1 (.clk(clk), .priem(Priem), .del4(delay4_1_del4));
endmodule

module ascii_to_bcd (
  input  [7:0] ASCII,
  output [3:0] BCD
);

  wire nand_1_out, nor_1_out, not_1_out, not_2_out, or_1_out;

  nand nand_1 (nand_1_out, ASCII[4], ASCII[5], not_1_out, not_2_out);
  not not_1 (not_1_out, ASCII[6]);
  not not_2 (not_2_out, ASCII[7]);
  nor nor_1 (nor_1_out, ASCII[0], ASCII[1], ASCII[2], ASCII[3], ASCII[4], ASCII[5], ASCII[6], ASCII[7]);
  or or_1 (or_1_out, nand_1_out, nor_1_out);
  or or_2 (BCD[0], ASCII[0], or_1_out);
  or or_3 (BCD[1], ASCII[1], or_1_out);
  or or_4 (BCD[2], ASCII[2], or_1_out);
  or or_5 (BCD[3], ASCII[3], or_1_out);
endmodule

module Comands (
  input  right_from_gate,
  input  [7:0] Trig_1,
  input  [7:0] Trig_2,
  input  [7:0] Trig_3,
  input  [7:0] Trig_4,
  input  clk,
  input  Priem,
  output Left_Cursor,
  output Right_Cursor,
  output Delete,
  output Enter
);

  wire and_1_out, and_2_out, and_3_out, and_4_out, and_5_out, and_6_out, and_7_out, and_8_out, and_9_out,
       and_10_out, and_11_out, and_12_out, and_13_out, and_14_out, and_15_out, delay3_1_del3, delay4_1_del4,
       not_1_out, not_2_out, not_3_out, not_4_out, not_5_out, not_6_out, not_7_out, not_8_out, not_9_out,
       not_10_out, not_11_out, not_12_out, not_13_out, not_14_out, not_15_out, not_16_out, not_17_out,
       not_18_out, not_19_out, not_20_out, not_21_out, not_22_out, not_23_out, not_24_out, not_25_out,
       not_26_out, not_27_out, not_28_out, not_29_out, not_30_out, not_31_out, not_32_out, not_33_out,
       not_34_out, not_35_out, not_36_out, not_37_out, not_38_out, not_39_out, not_40_out, not_41_out,
       not_42_out, not_43_out, not_44_out, not_45_out, not_46_out, not_47_out, not_48_out, not_49_out,
       not_50_out, not_51_out, or_1_out, or_2_out, or_3_out;

  not not_1 (not_1_out, Trig_1[7]);
  not not_2 (not_2_out, Trig_1[5]);
  not not_3 (not_3_out, Trig_1[4]);
  not not_4 (not_4_out, Trig_1[3]);
  not not_5 (not_5_out, Trig_1[1]);
  not not_6 (not_6_out, Trig_1[0]);
  not not_7 (not_7_out, Trig_1[7]);
  not not_8 (not_8_out, Trig_1[5]);
  not not_9 (not_9_out, Trig_1[4]);
  not not_10 (not_10_out, Trig_1[3]);
  not not_11 (not_11_out, Trig_1[2]);
  not not_12 (not_12_out, Trig_1[1]);
  not not_13 (not_13_out, Trig_1[7]);
  not not_14 (not_14_out, Trig_1[0]);
  not not_15 (not_15_out, Trig_1[7]);
  not not_16 (not_16_out, Trig_1[6]);
  not not_17 (not_17_out, Trig_1[4]);
  not not_18 (not_18_out, Trig_1[3]);
  not not_19 (not_19_out, Trig_1[2]);
  not not_20 (not_20_out, Trig_1[1]);
  not not_21 (not_21_out, Trig_1[0]);
  not not_22 (not_22_out, Trig_1[7]);
  not not_23 (not_23_out, Trig_1[6]);
  not not_24 (not_24_out, Trig_1[5]);
  not not_25 (not_25_out, Trig_1[4]);
  not not_26 (not_26_out, Trig_1[2]);
  not not_27 (not_27_out, Trig_1[1]);
  not not_28 (not_28_out, Trig_1[0]);
  not not_29 (not_29_out, Trig_1[7]);
  not not_30 (not_30_out, Trig_1[6]);
  not not_31 (not_31_out, Trig_1[5]);
  not not_32 (not_32_out, Trig_1[4]);
  not not_33 (not_33_out, Trig_1[1]);
  not not_34 (not_34_out, Trig_2[7]);
  not not_35 (not_35_out, Trig_2[5]);
  not not_36 (not_36_out, Trig_2[2]);
  and and_1 (and_1_out, not_1_out, Trig_1[6], not_2_out, not_3_out, not_4_out, Trig_1[2], not_5_out, not_6_out);
  and and_2 (and_2_out, not_7_out, Trig_1[6], not_8_out, not_9_out, not_10_out, not_11_out, not_12_out, Trig_1[0]);
  not not_37 (not_37_out, Trig_2[7]);
  not not_38 (not_38_out, Trig_2[6]);
  not not_39 (not_39_out, Trig_2[3]);
  not not_40 (not_40_out, Trig_2[2]);
  and and_3 (and_3_out, not_13_out, Trig_1[6], Trig_1[5], Trig_1[4], Trig_1[3], Trig_1[2], Trig_1[1], not_14_out);
  and and_4 (and_4_out, not_15_out, not_16_out, Trig_1[5], not_17_out, not_18_out, not_19_out, not_20_out, not_21_out);
  and and_5 (and_5_out, not_22_out, not_23_out, not_24_out, not_25_out, Trig_1[3], not_26_out, not_27_out, not_28_out);
  and and_6 (and_6_out, not_29_out, not_30_out, not_31_out, not_32_out, Trig_1[3], Trig_1[2], not_33_out, Trig_1[0]);
  and and_7 (and_7_out, not_34_out, Trig_2[6], not_35_out, Trig_2[4], Trig_2[3], not_36_out, Trig_2[1], Trig_2[0]);
  and and_8 (and_8_out, not_37_out, not_38_out, Trig_2[5], Trig_2[4], not_39_out, not_40_out, Trig_2[1], Trig_2[0]);
  not not_41 (not_41_out, Trig_3[7]);
  not not_42 (not_42_out, Trig_3[6]);
  not not_43 (not_43_out, Trig_3[5]);
  not not_44 (not_44_out, Trig_3[2]);
  not not_45 (not_45_out, Trig_3[7]);
  not not_46 (not_46_out, Trig_3[5]);
  not not_47 (not_47_out, Trig_3[2]);
  not not_48 (not_48_out, Trig_4[7]);
  not not_49 (not_49_out, Trig_4[6]);
  not not_50 (not_50_out, Trig_4[5]);
  not not_51 (not_51_out, Trig_4[2]);
  and and_9 (and_9_out, not_41_out, not_42_out, not_43_out, Trig_3[4], Trig_3[3], not_44_out, Trig_3[1], Trig_3[0]);
  and and_10 (and_10_out, not_45_out, Trig_3[6], not_46_out, Trig_3[4], Trig_3[3], not_47_out, Trig_3[1], Trig_3[0]);
  and and_11 (and_11_out, not_48_out, not_49_out, not_50_out, Trig_4[4], Trig_4[3], not_51_out, Trig_4[1], Trig_4[0]);
  and and_12 (and_12_out, and_9_out, and_7_out, and_2_out);
  and and_13 (and_13_out, and_9_out, and_7_out, and_1_out);
  and and_14 (and_14_out, and_11_out, and_10_out, and_8_out, and_3_out);
  or or_1 (or_1_out, and_13_out, and_5_out);
  or or_2 (or_2_out, and_12_out, right_from_gate, and_4_out);
  and and_15 (and_15_out, delay3_1_del3, ~delay4_1_del4);  // AND_Gate
  or or_3 (or_3_out, and_14_out, and_5_out);
  and and_16 (Enter, delay3_1_del3, and_6_out);
  delay3 delay3_1 (.clk(clk), .priem(Priem), .del3(delay3_1_del3));
  delay4 delay4_1 (.clk(clk), .priem(Priem), .del4(delay4_1_del4));
  and and_17 (Left_Cursor, or_1_out, and_15_out);
  and and_18 (Right_Cursor, or_2_out, and_15_out);
  and and_19 (Delete, or_3_out, delay4_1_del4);

  // Notes on the sheet:
  //   Курсор Влево
  //   Курсор вправо
  //   Delete 2
  //   Space
  //   BackSpace
  //   Enter
  //   CSI
  //   Delete 1
  //   ESC
  //   CSI
  //   ESC
  //   Delete
  //   Курсор влево
  //   Курсор вправо
endmodule

module to_save (
  input  [7:0] inp,
  input  ESC1,
  input  ESC2,
  input  ESC3,
  output YP,
  output YC
);

  wire and_1_out, and_2_out, and_3_out, and_4_out, and_5_out, and_6_out, and_7_out, and_8_out, and_9_out,
       not_1_out, not_2_out, not_3_out, not_4_out, not_5_out, not_6_out, not_7_out, not_8_out, not_9_out,
       not_10_out, not_11_out, not_12_out, not_13_out, not_14_out, not_15_out, not_16_out, not_17_out,
       not_18_out, not_19_out, not_20_out, not_21_out, not_22_out, not_23_out, not_24_out, not_25_out,
       not_26_out, not_27_out, not_28_out, not_29_out, not_30_out, not_31_out, not_32_out, not_33_out,
       not_34_out, not_35_out, not_36_out, not_37_out, not_38_out, not_39_out, not_40_out, not_41_out,
       not_42_out, not_43_out, not_44_out, not_45_out;

  not not_1 (not_1_out, inp[7]);
  not not_2 (not_2_out, inp[0]);
  not not_3 (not_3_out, inp[7]);
  not not_4 (not_4_out, inp[6]);
  not not_5 (not_5_out, inp[4]);
  not not_6 (not_6_out, inp[3]);
  not not_7 (not_7_out, inp[2]);
  not not_8 (not_8_out, inp[1]);
  not not_9 (not_9_out, inp[0]);
  not not_10 (not_10_out, inp[7]);
  not not_11 (not_11_out, inp[6]);
  not not_12 (not_12_out, inp[5]);
  not not_13 (not_13_out, inp[4]);
  not not_14 (not_14_out, inp[2]);
  not not_15 (not_15_out, inp[1]);
  not not_16 (not_16_out, inp[0]);
  not not_17 (not_17_out, inp[7]);
  not not_18 (not_18_out, inp[6]);
  not not_19 (not_19_out, inp[5]);
  not not_20 (not_20_out, inp[4]);
  not not_21 (not_21_out, inp[1]);
  not not_22 (not_22_out, inp[7]);
  not not_23 (not_23_out, inp[5]);
  not not_24 (not_24_out, inp[4]);
  not not_25 (not_25_out, inp[3]);
  not not_26 (not_26_out, inp[1]);
  not not_27 (not_27_out, inp[0]);
  not not_28 (not_28_out, inp[7]);
  not not_29 (not_29_out, inp[5]);
  not not_30 (not_30_out, inp[4]);
  not not_31 (not_31_out, inp[3]);
  not not_32 (not_32_out, inp[2]);
  not not_33 (not_33_out, inp[1]);
  not not_34 (not_34_out, inp[7]);
  not not_35 (not_35_out, inp[6]);
  not not_36 (not_36_out, inp[3]);
  not not_37 (not_37_out, inp[2]);
  and and_1 (and_1_out, not_1_out, inp[6], inp[5], inp[4], ESC3, inp[3], inp[2], inp[1], not_2_out);
  and and_2 (and_2_out, not_3_out, not_4_out, inp[5], not_5_out, not_6_out, not_7_out, not_8_out, not_9_out);
  and and_3 (and_3_out, not_10_out, not_11_out, not_12_out, not_13_out, inp[3], not_14_out, not_15_out, not_16_out);
  and and_4 (and_4_out, not_17_out, not_18_out, not_19_out, not_20_out, inp[3], inp[2], not_21_out, inp[0]);
  and and_5 (and_5_out, not_22_out, inp[6], not_23_out, not_24_out, ESC2, not_25_out, inp[2], not_26_out, not_27_out);
  and and_6 (and_6_out, not_28_out, inp[6], not_29_out, not_30_out, ESC2, not_31_out, not_32_out, not_33_out, inp[0]);
  and and_7 (and_7_out, not_34_out, not_35_out, inp[5], inp[4], ESC2, not_36_out, not_37_out, inp[1], inp[0]);
  not not_38 (not_38_out, inp[7]);
  not not_39 (not_39_out, inp[6]);
  not not_40 (not_40_out, inp[5]);
  not not_41 (not_41_out, inp[2]);
  not not_42 (not_42_out, inp[7]);
  not not_43 (not_43_out, inp[5]);
  not not_44 (not_44_out, inp[2]);
  nor nor_1 (YC, and_2_out, and_3_out, and_4_out);
  and and_8 (and_8_out, not_38_out, not_39_out, not_40_out, inp[4], inp[3], not_41_out, inp[1], inp[0]);
  and and_9 (and_9_out, not_42_out, inp[6], not_43_out, inp[4], ESC1, inp[3], not_44_out, inp[1], inp[0]);
  not not_45 (not_45_out, YC);
  or or_1 (YP, and_8_out, and_9_out, not_45_out, and_5_out, and_6_out, and_7_out, and_1_out);

  // Notes on the sheet:
  //   Space
  //   Enter
  //   Delete 2
  //   BackSpace
  //   Курсор Влево
  //   Курсор вправо
  //   Delete 1
  //   ESC
  //   CSI
endmodule

module delay2 (
  input  clk,
  input  priem,
  output del2
);

  wire and_1_out, and_2_out, d_ff_1_q, d_ff_1_qn, d_ff_2_q, d_ff_2_qn, not_1_out, not_2_out;

  not not_1 (not_1_out, del2);
  D_Flip_Flop d_ff_1 (.D(d_ff_1_qn), .clk(and_1_out), .Q(d_ff_1_q), .Qn(d_ff_1_qn), .reset(and_2_out));  // open: preset
  and and_1 (and_1_out, clk, not_1_out);
  D_Flip_Flop d_ff_2 (.D(d_ff_2_qn), .clk(d_ff_1_qn), .Q(d_ff_2_q), .Qn(d_ff_2_qn), .reset(and_2_out));  // open: preset
  and and_2 (and_2_out, priem, del2);
  not not_2 (not_2_out, d_ff_1_q);
  and and_3 (del2, not_2_out, d_ff_2_q);
endmodule

module delay3 (
  input  clk,
  input  priem,
  output del3
);

  wire and_1_out, and_2_out, d_ff_1_q, d_ff_1_qn, d_ff_2_q, d_ff_2_qn, not_1_out;

  D_Flip_Flop d_ff_1 (.D(d_ff_1_qn), .clk(and_1_out), .Q(d_ff_1_q), .Qn(d_ff_1_qn), .reset(and_2_out));  // open: preset
  and and_1 (and_1_out, clk, not_1_out);
  not not_1 (not_1_out, del3);
  D_Flip_Flop d_ff_2 (.D(d_ff_2_qn), .clk(d_ff_1_qn), .Q(d_ff_2_q), .Qn(d_ff_2_qn), .reset(and_2_out));  // open: preset
  and and_2 (and_2_out, priem, del3);
  and and_3 (del3, d_ff_1_q, d_ff_2_q);
endmodule

module Generator (
  input  gen_in,
  input  Priem_in,
  output clk,
  output Priem_out
);

  wire and_2_out, and_3_out, D0_q, D0_qn, D1_q, D1_qn, D2_q, D2_qn, not_1_out, not_2_out, not_4_out;

  not not_1 (not_1_out, and_3_out);
  and and_1 (clk, gen_in, Priem_in, not_2_out);
  not not_2 (not_2_out, and_3_out);
  and and_2 (and_2_out, gen_in, not_1_out);
  D_Flip_Flop D0 (.D(D0_qn), .clk(and_2_out), .Q(D0_q), .Qn(D0_qn), .reset(Priem_out));  // open: preset
  not not_3 (Priem_out, Priem_in);
  D_Flip_Flop D1 (.D(D1_qn), .clk(D0_qn), .Q(D1_q), .Qn(D1_qn), .reset(Priem_out));  // open: preset
  D_Flip_Flop D2 (.D(D2_qn), .clk(D1_qn), .Q(D2_q), .Qn(D2_qn), .reset(Priem_out));  // open: preset
  not not_4 (not_4_out, D0_q);
  and and_3 (and_3_out, not_4_out, D1_q, D2_q);
endmodule

module delay4 (
  input  clk,
  input  priem,
  output del4
);

  wire and_1_out, and_2_out, d_ff_1_q, d_ff_1_qn, d_ff_2_q, d_ff_2_qn, d_ff_3_q, d_ff_3_qn, not_1_out,
       not_2_out, not_3_out;

  not not_1 (not_1_out, del4);
  D_Flip_Flop d_ff_1 (.D(d_ff_1_qn), .clk(and_1_out), .Q(d_ff_1_q), .Qn(d_ff_1_qn), .reset(and_2_out));  // open: preset
  and and_1 (and_1_out, clk, not_1_out);
  D_Flip_Flop d_ff_2 (.D(d_ff_2_qn), .clk(d_ff_1_qn), .Q(d_ff_2_q), .Qn(d_ff_2_qn), .reset(and_2_out));  // open: preset
  D_Flip_Flop d_ff_3 (.D(d_ff_3_qn), .clk(d_ff_2_qn), .Q(d_ff_3_q), .Qn(d_ff_3_qn), .reset(and_2_out));  // open: preset
  not not_2 (not_2_out, d_ff_1_q);
  not not_3 (not_3_out, d_ff_2_q);
  and and_2 (and_2_out, priem, del4);
  and and_3 (del4, not_2_out, not_3_out, d_ff_3_q);
endmodule

module delay1 (
  input  clk,
  input  priem,
  output del1
);

  wire and_1_out, and_2_out, d_ff_1_qn, not_1_out;

  D_Flip_Flop d_ff_1 (.D(d_ff_1_qn), .clk(and_1_out), .Q(del1), .Qn(d_ff_1_qn), .reset(and_2_out));  // open: preset
  and and_1 (and_1_out, clk, not_1_out);
  not not_1 (not_1_out, del1);
  and and_2 (and_2_out, priem, del1);
endmodule

module Cont_seq (
  input  [7:0] Trig_1,
  input  [7:0] Trig_2,
  input  [7:0] Trig_3,
  input  clk,
  input  Priem,
  output ESC1,
  output ESC2,
  output ESC3
);

  wire and_1_out, and_2_out, and_3_out, and_4_out, and_5_out, and_6_out, and_7_out, and_8_out, and_9_out,
       and_10_out, and_11_out, and_12_out, and_13_out, and_14_out, delay5_1_del5, nor_1_out, not_1_out,
       not_2_out, not_3_out, not_4_out, not_5_out, not_6_out, not_7_out, not_8_out, not_9_out, not_10_out,
       not_11_out, not_12_out, not_13_out, not_14_out, not_15_out, not_16_out, not_17_out, not_18_out,
       not_19_out, not_20_out, not_21_out, not_22_out, or_1_out, or_2_out, or_3_out;

  not not_1 (not_1_out, Trig_1[7]);
  not not_2 (not_2_out, Trig_1[6]);
  not not_3 (not_3_out, Trig_1[5]);
  not not_4 (not_4_out, Trig_1[2]);
  not not_5 (not_5_out, Trig_1[7]);
  not not_6 (not_6_out, Trig_1[6]);
  not not_7 (not_7_out, Trig_1[3]);
  not not_8 (not_8_out, Trig_1[2]);
  not not_9 (not_9_out, Trig_1[7]);
  not not_10 (not_10_out, Trig_1[5]);
  not not_11 (not_11_out, Trig_1[2]);
  and and_1 (and_1_out, not_1_out, not_2_out, not_3_out, Trig_1[4], Trig_1[3], not_4_out, Trig_1[1], Trig_1[0]);
  and and_2 (and_2_out, not_5_out, not_6_out, Trig_1[5], Trig_1[4], not_7_out, not_8_out, Trig_1[1], Trig_1[0]);
  and and_3 (and_3_out, not_9_out, Trig_1[6], not_10_out, Trig_1[4], Trig_1[3], not_11_out, Trig_1[1], Trig_1[0]);
  not not_12 (not_12_out, Trig_2[7]);
  not not_13 (not_13_out, Trig_2[6]);
  not not_14 (not_14_out, Trig_2[5]);
  and and_4 (and_4_out, not_12_out, not_13_out, not_14_out, Trig_2[4], Trig_2[3], not_15_out, Trig_2[1], Trig_2[0]);
  not not_15 (not_15_out, Trig_2[2]);
  not not_16 (not_16_out, Trig_2[7]);
  not not_17 (not_17_out, Trig_2[5]);
  and and_5 (and_5_out, not_16_out, Trig_2[6], not_17_out, Trig_2[4], Trig_2[3], not_18_out, Trig_2[1], Trig_2[0]);
  not not_18 (not_18_out, Trig_2[2]);
  not not_19 (not_19_out, Trig_3[7]);
  not not_20 (not_20_out, Trig_3[6]);
  not not_21 (not_21_out, Trig_3[5]);
  not not_22 (not_22_out, Trig_3[2]);
  and and_6 (and_6_out, and_4_out, and_3_out);
  and and_7 (and_7_out, not_19_out, not_20_out, not_21_out, Trig_3[4], Trig_3[3], not_22_out, Trig_3[1], Trig_3[0]);
  and and_8 (and_8_out, and_7_out, and_5_out, and_2_out);
  nor nor_1 (nor_1_out, and_8_out, and_6_out, and_1_out);
  delay5 delay5_1 (.clk(clk), .priem(Priem), .del5(delay5_1_del5));
  or or_1 (or_1_out, and_6_out, and_8_out, nor_1_out);
  or or_2 (or_2_out, and_1_out, and_8_out, nor_1_out);
  or or_3 (or_3_out, and_1_out, and_6_out, nor_1_out);
  and and_9 (and_9_out, and_1_out, delay5_1_del5);
  D_Flip_Flop d_ff_1 (.Q(ESC1), .preset(and_9_out), .reset(and_10_out));  // open: D, clk, Qn
  and and_10 (and_10_out, or_1_out, delay5_1_del5);
  and and_11 (and_11_out, and_6_out, delay5_1_del5);
  D_Flip_Flop d_ff_2 (.Q(ESC2), .preset(and_11_out), .reset(and_12_out));  // open: D, clk, Qn
  and and_12 (and_12_out, or_2_out, delay5_1_del5);
  and and_13 (and_13_out, and_8_out, delay5_1_del5);
  D_Flip_Flop d_ff_3 (.Q(ESC3), .preset(and_13_out), .reset(and_14_out));  // open: D, clk, Qn
  and and_14 (and_14_out, or_3_out, delay5_1_del5);

  // Notes on the sheet:
  //   ESC
  //   Delete 1
  //   CSI
  //   ESC
  //   CSI
  //   ESC
endmodule

module delay5 (
  input  clk,
  input  priem,
  output del5
);

  wire and_1_out, and_2_out, d_ff_1_q, d_ff_1_qn, d_ff_2_q, d_ff_2_qn, d_ff_3_q, d_ff_3_qn, not_1_out,
       not_2_out;

  not not_1 (not_1_out, del5);
  D_Flip_Flop d_ff_1 (.D(d_ff_1_qn), .clk(and_1_out), .Q(d_ff_1_q), .Qn(d_ff_1_qn), .reset(and_2_out));  // open: preset
  and and_1 (and_1_out, clk, not_1_out);
  D_Flip_Flop d_ff_2 (.D(d_ff_2_qn), .clk(d_ff_1_qn), .Q(d_ff_2_q), .Qn(d_ff_2_qn), .reset(and_2_out));  // open: preset
  D_Flip_Flop d_ff_3 (.D(d_ff_3_qn), .clk(d_ff_2_qn), .Q(d_ff_3_q), .Qn(d_ff_3_qn), .reset(and_2_out));  // open: preset
  not not_2 (not_2_out, d_ff_2_q);
  and and_2 (and_2_out, priem, del5);
  and and_3 (del5, d_ff_1_q, not_2_out, d_ff_3_q);
endmodule
